# Fritzing sketch testing-noBB (saved by Fritzing 0.9.2b)

parts:
  Raspberry_Pi1 = Raspberry Pi 2
  MOTOR1 = Vibration Motor
  Part2 = SRF05
  R1 = Resistor [tolerance=±5% resistance=2.2k package="2010 [SMD]"]
  R2 = Resistor [tolerance=±5% resistance=1.2k package="2010 [SMD]"]

nets:
  N1: Raspberry_Pi1.GPIO4, Part2.Trig
  GND: Raspberry_Pi1.GND, MOTOR1.NEG, Part2.GND, R1.Pin_1
  N2: Raspberry_Pi1.GPIO17, R2.Pin_1
  N3: Raspberry_Pi1.GPIO14, MOTOR1.POS
  5V: Raspberry_Pi1.5V, Part2.VCC
  N4: Part2.Echo, R2.Pin_0

custom parts:
  Vibration Motor: An eccentric vibration motor!
