# Fritzing sketch testing-vibro (saved by Fritzing 0.9.2b)

parts:
  Raspberry_Pi1 = Raspberry Pi 2
  MOTOR1 = Vibration Motor

nets:
  N1: Raspberry_Pi1.3v3, MOTOR1.POS
  N2: Raspberry_Pi1.GND, MOTOR1.NEG

custom parts:
  Vibration Motor: An eccentric vibration motor!
