# Fritzing sketch testing-usd (saved by Fritzing 0.9.2b)
breadboards: 1

parts:
  Part1 = SRF05
  Raspberry_Pi1 = Raspberry Pi 2
  R2 = Resistor [tolerance=±5% resistance=2.2k package="1206 [SMD]"]
  R1 = Resistor [tolerance=±5% resistance=1.2k package="2512 [SMD]"]
  MOTOR1 = Vibration Motor

nets:
  VCC: Part1.VCC, Raspberry_Pi1.5V
  N1: Part1.Trig, Raspberry_Pi1.GPIO4
  N2: Part1.Echo, R1.Pin_0
  GND: Part1.GND, Raspberry_Pi1.GND, R2.Pin_0, MOTOR1.NEG
  N3: Raspberry_Pi1.GPIO17, R2.Pin_1, R1.Pin_1
  N4: Raspberry_Pi1.GPIO14, MOTOR1.POS

custom parts:
  Vibration Motor: An eccentric vibration motor!
